// Digital circuit 10.dig as structural Verilog
module _10 (
  input  in_1,
  input  in_6,
  input  in_7,
  input  in_13,
  output out_2,
  output out_3,
  output out_4,
  output out_5,
  output out_8,
  output out_9,
  output out_10,
  output out_11,
  output out_12,
  output out_14,
  output out_15,
  output out_16,
  output out_17
);

  wire and_1_out, and_2_out, and_3_out, d_ff_1_nq, d_ff_2_nq, d_ff_3_nq, d_ff_4_nq, d_ff_8_nq;

  D_FF d_ff_1 (.D(d_ff_1_nq), .C(in_1), .Q(out_5), .nQ(d_ff_1_nq));
  D_FF d_ff_2 (.D(d_ff_2_nq), .C(out_5), .Q(out_4), .nQ(d_ff_2_nq));
  D_FF d_ff_3 (.D(d_ff_3_nq), .C(out_4), .Q(out_3), .nQ(d_ff_3_nq));
  D_FF d_ff_4 (.D(d_ff_4_nq), .C(out_3), .Q(out_2), .nQ(d_ff_4_nq));
  JK_FF jk_ff_1 (.J(in_7), .C(in_6), .K(in_7), .Q(out_12));  // open: nQ
  and and_1 (and_1_out, out_12, in_7);
  and and_2 (and_2_out, out_11, and_1_out);
  JK_FF jk_ff_2 (.J(and_1_out), .C(in_6), .K(and_1_out), .Q(out_11));  // open: nQ
  JK_FF jk_ff_3 (.J(and_2_out), .C(in_6), .K(and_2_out), .Q(out_10));  // open: nQ
  and and_3 (and_3_out, out_10, and_2_out);
  JK_FF jk_ff_4 (.J(and_3_out), .C(in_6), .K(and_3_out), .Q(out_9));  // open: nQ
  and and_4 (out_8, out_9, and_3_out);
  D_FF d_ff_5 (.D(d_ff_8_nq), .C(in_13), .Q(out_17));  // open: nQ
  D_FF d_ff_6 (.D(out_17), .C(in_13), .Q(out_16));  // open: nQ
  D_FF d_ff_7 (.D(out_16), .C(in_13), .Q(out_15));  // open: nQ
  D_FF d_ff_8 (.D(out_15), .C(in_13), .Q(out_14), .nQ(d_ff_8_nq));
endmodule
