// Digital circuit 12.dig as structural Verilog
module _12 (
  input  in_1,
  input  in_2,
  input  in_7,
  input  in_8,
  input  in_9,
  input  in_10,
  input  in_11,
  input  in_12,
  output out_3,
  output out_4,
  output out_5,
  output out_6
);

  wire _7483_1_p12, _7483_1_p13, _7483_1_p14, _7483_1_p15, _7483_2_p12, _7483_2_p13, _7483_2_p14,
       _7483_2_p15, _7483_3_p12, _7483_3_p13, _7483_3_p14, _7483_3_p15, and_1_out, and_2_out, and_3_out,
       and_4_out, not_1_out, not_2_out, or_1_out, xor_1_out, xor_2_out, xor_3_out, xor_4_out;

  xor xor_1 (xor_1_out, in_2, in_1);
  and and_1 (and_1_out, in_1, in_2);
  xor xor_2 (xor_2_out, in_8, in_7);
  and and_2 (and_2_out, in_7, in_8);
  xor xor_3 (xor_3_out, in_10, in_9);
  and and_3 (and_3_out, in_9, in_10);
  xor xor_4 (xor_4_out, in_12, in_11);
  and and_4 (and_4_out, in_11, in_12);
  // _7483 _7483_1: pin names not known; wires that end beside it: 1'b0, xor_1_out, and_1_out, 1'b0, 1'b0, xor_2_out, and_2_out, 1'b0, 1'b0, 1'b1, 1'b0, _7483_1_p12, _7483_1_p13, _7483_1_p14, _7483_1_p15, out_4
  // _7483 _7483_2: pin names not known; wires that end beside it: 1'b0, xor_3_out, and_3_out, 1'b0, 1'b0, and_4_out, xor_4_out, 1'b0, 1'b0, 1'b1, 1'b0, _7483_2_p12, _7483_2_p13, _7483_2_p14, _7483_2_p15, out_5
  // _7483 _7483_3: pin names not known; wires that end beside it: 1'b0, _7483_1_p12, _7483_1_p13, _7483_1_p14, _7483_1_p15, _7483_2_p12, _7483_2_p13, _7483_2_p14, _7483_2_p15, 1'b1, 1'b0, _7483_3_p12, _7483_3_p13, _7483_3_p14, _7483_3_p15, out_6
  or or_1 (or_1_out, _7483_3_p14, _7483_3_p15);
  not not_1 (not_1_out, _7483_3_p12);
  not not_2 (not_2_out, _7483_3_p13);
  and and_5 (out_3, not_1_out, or_1_out, not_2_out);
endmodule
