// Digital circuit 2.dig as structural Verilog
module _2 (
  input  in_1,
  input  in_2,
  input  in_4,
  input  in_5,
  output out_3,
  output out_6
);

  wire nand_1_out, nand_2_out, nand_3_out;

  nand nand_1 (nand_1_out, in_2, in_1);
  nand nand_2 (nand_2_out, in_4, in_4);
  nand nand_3 (nand_3_out, in_5, in_5);
  nand nand_4 (out_6, nand_2_out, nand_3_out);
  nand nand_5 (out_3, nand_1_out, nand_1_out);
endmodule
