// Digital circuit 3.dig as structural Verilog
module _3 (
  input  in_1,
  input  in_2,
  input  in_3,
  input  in_4,
  input  in_9,
  input  in_10,
  input  in_11,
  input  in_12,
  output out_5,
  output out_6,
  output out_7,
  output out_8,
  output out_13,
  output out_14,
  output out_15,
  output out_16
);

  xor xor_1 (out_5, in_1, in_2);
  xor xor_2 (out_6, in_2, in_3);
  xor xor_3 (out_7, in_3, in_4);
  xor xor_4 (out_13, in_9, out_14);
  xor xor_5 (out_14, in_10, out_15);
  xor xor_6 (out_15, in_11, in_12);

  assign out_8 = in_4;
  assign out_16 = in_12;
endmodule
