// Digital circuit 4.dig as structural Verilog
module _4 (
  input  clk
);

  wire _7448_1_pin9, _7448_1_pin10, _7448_1_pin11, _7448_1_pin13, _7448_1_pin14, _7448_1_pin15, d_ff_1_nq,
       d_ff_1_q, d_ff_2_nq, d_ff_2_q, d_ff_3_nq, d_ff_3_q, d_ff_4_nq, d_ff_4_q, undriven;

  D_FF d_ff_1 (.D(d_ff_1_nq), .C(clk), .Q(d_ff_1_q), .nQ(d_ff_1_nq));
  D_FF d_ff_2 (.D(d_ff_2_nq), .C(d_ff_1_q), .Q(d_ff_2_q), .nQ(d_ff_2_nq));
  D_FF d_ff_3 (.D(d_ff_3_nq), .C(d_ff_2_q), .Q(d_ff_3_q), .nQ(d_ff_3_nq));
  D_FF d_ff_4 (.D(d_ff_4_nq), .C(d_ff_3_q), .Q(d_ff_4_q), .nQ(d_ff_4_nq));
  _7448 _7448_1 (
    .pin1(d_ff_2_q), .pin2(d_ff_3_q), .pin3(1'b1), .pin4(1'b1), .pin5(1'b1), .pin6(d_ff_4_q),
    .pin7(d_ff_1_q), .pin8(1'b0), .pin9(_7448_1_pin9), .pin10(_7448_1_pin10), .pin11(_7448_1_pin11),
    .pin13(_7448_1_pin13), .pin14(_7448_1_pin14), .pin15(_7448_1_pin15), .pin16(1'b1));  // open: pin12
  Seven_Seg seven_seg_1 (
    .a(_7448_1_pin13), .b(undriven), .c(_7448_1_pin11), .d(_7448_1_pin10), .e(_7448_1_pin9),
    .f(_7448_1_pin15), .g(_7448_1_pin14), .dp(1'b0));
  // _7448 _7448_2: pin names not known
endmodule
