// Digital circuit 5.dig as structural Verilog
module _5 (
  input  in_1,
  input  in_2,
  input  in_3,
  input  in_8,
  input  in_9,
  input  in_10,
  output out_4,
  output out_5,
  output out_6,
  output out_7,
  output out_11,
  output out_12,
  output out_13,
  output out_14
);

  wire and_5_out, and_6_out, and_7_out, and_8_out, not_1_out, not_2_out, not_3_out, not_4_out, not_5_out,
       not_6_out, not_7_out, not_8_out;

  not not_1 (not_1_out, in_9);
  not not_2 (not_2_out, in_10);
  and and_1 (out_11, not_1_out, not_2_out);
  and and_2 (out_12, not_1_out, in_10);
  and and_3 (out_13, in_9, not_2_out);
  and and_4 (out_14, in_9, in_10);
  not not_3 (not_3_out, in_1);
  not not_4 (not_4_out, in_2);
  and and_5 (and_5_out, not_3_out, not_4_out);
  and and_6 (and_6_out, not_3_out, in_2);
  and and_7 (and_7_out, in_1, not_4_out);
  and and_8 (and_8_out, in_1, in_2);
  not not_5 (not_5_out, in_3);
  not not_6 (not_6_out, in_3);
  not not_7 (not_7_out, in_3);
  not not_8 (not_8_out, in_3);
  and and_9 (out_4, and_5_out, not_5_out);
  and and_10 (out_5, and_6_out, not_6_out);
  and and_11 (out_6, and_7_out, not_7_out);
  and and_12 (out_7, and_8_out, not_8_out);
endmodule
