// Digital circuit 7.dig as structural Verilog
module _7 (
  input  in_1,
  input  in_2,
  input  in_3,
  input  in_4,
  input  in_5,
  input  in_6,
  output out_7
);

  wire and_1_out, and_2_out, and_3_out, and_4_out, and_5_out, and_6_out, and_7_out, and_8_out, not_1_out,
       not_2_out, or_1_out, or_2_out;

  not not_1 (not_1_out, in_5);
  and and_1 (and_1_out, in_1, not_1_out);
  and and_2 (and_2_out, in_2, not_1_out);
  and and_3 (and_3_out, in_3, in_5);
  and and_4 (and_4_out, in_4, in_5);
  not not_2 (not_2_out, in_6);
  and and_5 (and_5_out, and_1_out, not_2_out);
  and and_6 (and_6_out, and_2_out, in_6);
  and and_7 (and_7_out, and_3_out, not_2_out);
  and and_8 (and_8_out, and_4_out, in_6);
  or or_1 (or_1_out, and_5_out, and_6_out);
  or or_2 (or_2_out, and_7_out, and_8_out);
  or or_3 (out_7, or_1_out, or_2_out);
endmodule
