// Digital circuit 8.dig as structural Verilog
module _8 (
  input  in_1,
  input  in_2,
  input  in_5,
  input  in_6,
  input  in_7,
  input  in_10,
  input  in_11,
  input  in_12,
  output out_3,
  output out_4,
  output out_8,
  output out_9,
  output out_13,
  output out_14
);

  wire _74238_1_pin7, _74238_1_pin9, _74238_1_pin10, _74238_1_pin11, _74238_1_pin12, _74238_1_pin13,
       _74238_1_pin14, and_2_out, and_3_out, or_2_out, or_3_out, or_4_out, or_5_out, xor_2_out;

  xor xor_1 (out_3, in_1, in_2);
  and and_1 (out_4, in_1, in_2);
  xor xor_2 (xor_2_out, in_5, in_6);
  and and_2 (and_2_out, in_5, in_6);
  xor xor_3 (out_8, xor_2_out, in_7);
  and and_3 (and_3_out, xor_2_out, in_7);
  or or_1 (out_9, and_3_out, and_2_out);
  _74238 _74238_1 (
    .pin1(in_10), .pin2(in_11), .pin3(in_12), .pin4(1'b0), .pin5(1'b0), .pin6(1'b1), .pin7(_74238_1_pin7),
    .pin8(1'b0), .pin9(_74238_1_pin9), .pin10(_74238_1_pin10), .pin11(_74238_1_pin11),
    .pin12(_74238_1_pin12), .pin13(_74238_1_pin13), .pin14(_74238_1_pin14), .pin16(1'b1));  // open: pin15
  or or_2 (or_2_out, _74238_1_pin14, _74238_1_pin13);
  or or_3 (or_3_out, _74238_1_pin11, _74238_1_pin7);
  or or_4 (or_4_out, _74238_1_pin12, _74238_1_pin10);
  or or_5 (or_5_out, _74238_1_pin9, _74238_1_pin7);
  or or_6 (out_13, or_2_out, or_3_out);
  or or_7 (out_14, or_4_out, or_5_out);
  // _7483 _7483_1: pin names not known; wires that end beside it: 1'b1
endmodule
