// Digital circuit 9.dig as structural Verilog
module _9 (
  input  in_1,
  input  in_2,
  input  in_3,
  input  in_6,
  input  in_9,
  input  in_12,
  input  in_13,
  input  in_14,
  output out_4,
  output out_5,
  output out_7,
  output out_8,
  output out_10,
  output out_11
);

  wire and_1_out, and_2_out, nand_1_out, nand_2_out, nand_5_out, nand_6_out, nand_9_out, nand_10_out,
       not_1_out, not_2_out, not_3_out, or_1_out;

  nand nand_1 (nand_1_out, in_1, in_3);
  nand nand_2 (nand_2_out, in_3, in_2);
  nand nand_3 (out_4, nand_1_out, out_5);
  nand nand_4 (out_5, out_4, nand_2_out);
  not not_1 (not_1_out, in_9);
  nand nand_5 (nand_5_out, not_1_out, in_6);
  nand nand_6 (nand_6_out, in_9, in_6);
  nand nand_7 (out_7, nand_5_out, out_8);
  nand nand_8 (out_8, out_7, nand_6_out);
  not not_2 (not_2_out, in_13);
  and and_1 (and_1_out, out_11, in_12);
  and and_2 (and_2_out, not_2_out, out_10);
  or or_1 (or_1_out, and_1_out, and_2_out);
  not not_3 (not_3_out, or_1_out);
  nand nand_9 (nand_9_out, or_1_out, in_14);
  nand nand_10 (nand_10_out, in_14, not_3_out);
  nand nand_11 (out_10, nand_9_out, out_11);
  nand nand_12 (out_11, out_10, nand_10_out);
endmodule
